# Fritzing sketch AdvancedBlink (saved by Fritzing 0.9.3b)
breadboards: 1

parts:
  LED1 = smd LED [color="Red (633nm)" package="1206 [SMD]"]  # not connected
  Part1 = Arduino Uno (Rev3) - ICSP
  U1 = POT [package=pot_mammoth]

nets:
  N1: Part1.5V, U1.E
